# Fritzing sketch SBAQC_1.0 (saved by Fritzing 0.9.3b)
breadboards: 1

parts:
  DS3231 = ZS-042 RTC Module
  PWM1 = PCA9685 16x12-bit PWM Breakout
  R3 = Resistor [tolerance=±5% resistance=10k package=THT]
  LM2596S = RioRand LM2596
  WeMos_D1_Mini1 = WeMos D1 Mini
  R1 = Resistor [tolerance=±5% resistance=10k package=THT]
  R2 = Resistor [tolerance=±5% resistance=10k package=THT]
  Micro_SD_Card = MicroSD Card Module
  DS3233 = DS18B20 1-Wire Temperature Sensor [part_number=DS18B20]

nets (from the schematic view):
  GND: DS3231.GND, PWM1.no_name_yet#501, LM2596S.Pin_3, WeMos_D1_Mini1.G, Micro_SD_Card.GND, DS3233.GND
  VCC: DS3231.VCC, PWM1.no_name_yet#505, R3.Pin_0, LM2596S.Pin_2, WeMos_D1_Mini1.5V, R1.Pin_0, R2.Pin_1, Micro_SD_Card.VCC, DS3233.VDD
  N1: DS3231.SDA, PWM1.no_name_yet#504, WeMos_D1_Mini1.D1, R1.Pin_1
  N2: DS3231.SCL, PWM1.no_name_yet#503, WeMos_D1_Mini1.D2, R2.Pin_0
  N3: R3.Pin_1, WeMos_D1_Mini1.D4, DS3233.DQ
  N4: WeMos_D1_Mini1.D5, Micro_SD_Card.SCK
  N5: WeMos_D1_Mini1.D6, Micro_SD_Card.MISO
  N6: WeMos_D1_Mini1.D7, Micro_SD_Card.MOSI
  N7: WeMos_D1_Mini1.D8, Micro_SD_Card.CS
